// Logisim project ProjectBusLayout.circ as structural Verilog: 14 circuits, main circuit Computer
module Computer (
);

  wire buzzer_1_p2, clock_1_out, clock_2_out, clock_3_out, cpu_1_buswriteenable,
       joystickcontroller_1_writeenabletobus, keyboard_1_avail, keyboardcontroller_1_keyboardread,
       keyboardcontroller_1_writetobus, ledpanelcontroller_1_leds, ledpanelcontroller_1_out_5,
       ledpanelcontroller_1_out_6, ledpanelcontroller_1_out_7, ledpanelcontroller_1_out_8,
       ledpanelcontroller_1_out_9, ledpanelcontroller_1_out_10, ledpanelcontroller_1_out_11,
       memorycontroller_1_writeenabletomem, memorycontroller_1_writetobus, rgb_video_1_p1, rgb_video_1_p2,
       terminalcontroller_1_writetoterminal;
  wire [3:0] undriven, undriven_2;
  wire [6:0] buzzer_1_p3, buzzercontroller_1_volumedata2, buzzercontroller_1_volumedata3, keyboard_1_data,
       terminalcontroller_1_datatoterminal;
  wire [7:0] rgb_video_1_p3, rgb_video_1_p4;
  wire [13:0] buzzer_1_p1, buzzercontroller_1_frequencydata2, buzzercontroller_1_frequencydata3;
  wire [23:0] memorycontroller_1_addresstomem, rgb_video_1_p5;
  wire [25:0] cpu_1_addresstobus;
  wire [31:0] controlled_buffer_1_out, cpu_1_datatobus, joystickcontroller_1_datatobus,
       keyboardcontroller_1_datatobus, memorycontroller_1_datatobus, memorycontroller_1_datatomem, ram_1_dout;

  RAM #(.addrWidth(24), .dataWidth(32), .enables("line")) ram_1 (
    .addr(memorycontroller_1_addresstomem), .we(memorycontroller_1_writeenabletomem), .clk(clock_1_out),
    .din(memorycontroller_1_datatomem), .dout(ram_1_dout));
  Clock clock_1 (.out(clock_1_out));
  Joystick joystick_1 ();  // open: x, y
  Clock clock_2 (.out(clock_2_out));
  Keyboard keyboard_1 (
    .clk(clock_2_out), .re(keyboardcontroller_1_keyboardread), .avail(keyboard_1_avail),
    .data(keyboard_1_data));  // open: clr
  MemoryController memorycontroller_1 (
    .WriteEnableFromBus(cpu_1_buswriteenable), .AddressFromBus(cpu_1_addresstobus),
    .DataFromBus(controlled_buffer_1_out), .DataFromMem(ram_1_dout),
    .DataToBus(memorycontroller_1_datatobus), .WriteToBus(memorycontroller_1_writetobus),
    .WriteEnableToMem(memorycontroller_1_writeenabletomem), .AddressToMem(memorycontroller_1_addresstomem),
    .DataToMem(memorycontroller_1_datatomem));
  CPU cpu_1 (
    .DataFromBus(controlled_buffer_1_out), .AddressToBus(cpu_1_addresstobus),
    .BusWriteEnable(cpu_1_buswriteenable), .DataToBus(cpu_1_datatobus));
  assign controlled_buffer_1_out = memorycontroller_1_writetobus ? memorycontroller_1_datatobus : 32'bz;  // Controlled_Buffer controlled_buffer_1
  assign controlled_buffer_1_out = cpu_1_buswriteenable ? cpu_1_datatobus : 32'bz;  // Controlled_Buffer controlled_buffer_2
  KeyboardController keyboardcontroller_1 (
    .KeyboardData(keyboard_1_data), .WriteEnableFromBus(cpu_1_buswriteenable),
    .KeyboardStatus(keyboard_1_avail), .AddressFromBus(cpu_1_addresstobus),
    .DataFromBus(controlled_buffer_1_out), .KeyboardRead(keyboardcontroller_1_keyboardread),
    .DataToBus(keyboardcontroller_1_datatobus), .WriteToBus(keyboardcontroller_1_writetobus));
  assign controlled_buffer_1_out = keyboardcontroller_1_writetobus ? keyboardcontroller_1_datatobus : 32'bz;  // Controlled_Buffer controlled_buffer_3
  assign controlled_buffer_1_out = joystickcontroller_1_writeenabletobus ? joystickcontroller_1_datatobus : 32'bz;  // Controlled_Buffer controlled_buffer_4
  JoyStickController joystickcontroller_1 (
    .WriteEnableFromBus(cpu_1_buswriteenable), .AddressFromBus(cpu_1_addresstobus), .X(undriven),
    .Y(undriven_2), .DataFromBus(controlled_buffer_1_out), .DataToBus(joystickcontroller_1_datatobus),
    .WriteEnableToBus(joystickcontroller_1_writeenabletobus));
  Clock clock_3 (.out(clock_3_out));
  TTY tty_1 (
    .data(terminalcontroller_1_datatoterminal), .clk(clock_3_out), .we(terminalcontroller_1_writetoterminal));  // open: clr
  // RGB_Video #(.height(256), .scale(1), .width(256)) rgb_video_1: pin names not known; wires that end beside it: rgb_video_1_p1, rgb_video_1_p2, rgb_video_1_p3, rgb_video_1_p4, rgb_video_1_p5
  Clock clock_4 (.out(rgb_video_1_p1));
  TerminalController terminalcontroller_1 (
    .WriteEnableFromBus(cpu_1_buswriteenable), .AddressFromBus(cpu_1_addresstobus),
    .DataFromBus(controlled_buffer_1_out), .DataToTerminal(terminalcontroller_1_datatoterminal),
    .WriteToTerminal(terminalcontroller_1_writetoterminal));
  RGBController rgbcontroller_1 (
    .AddressFromBus(cpu_1_addresstobus), .DataFromBus(controlled_buffer_1_out),
    .WriteEnable(cpu_1_buswriteenable), .RGBX(rgb_video_1_p3), .RGBY(rgb_video_1_p4),
    .RGBColor(rgb_video_1_p5), .RGBWrite(rgb_video_1_p2));
  // Buzzer buzzer_1: pin names not known; wires that end beside it: buzzer_1_p1, buzzer_1_p2, buzzer_1_p3
  BuzzerController buzzercontroller_1 (
    .DataFromBus(controlled_buffer_1_out), .WriteEnableFromBus(cpu_1_buswriteenable),
    .AddressFromBus(cpu_1_addresstobus), .FrequencyData1(buzzer_1_p1),
    .FrequencyData2(buzzercontroller_1_frequencydata2), .FrequencyData3(buzzercontroller_1_frequencydata3),
    .WriteToBuzzer(buzzer_1_p2), .VolumeData1(buzzer_1_p3), .VolumeData2(buzzercontroller_1_volumedata2),
    .VolumeData3(buzzercontroller_1_volumedata3));
  LedBar ledbar_1 (
    .led0(ledpanelcontroller_1_leds), .led1(ledpanelcontroller_1_out_5), .led2(ledpanelcontroller_1_out_6),
    .led3(ledpanelcontroller_1_out_7), .led4(ledpanelcontroller_1_out_8), .led5(ledpanelcontroller_1_out_9),
    .led6(ledpanelcontroller_1_out_10), .led7(ledpanelcontroller_1_out_11));
  LEDPanelController ledpanelcontroller_1 (
    .DataFromBus(controlled_buffer_1_out), .WriteEnableFromBus(cpu_1_buswriteenable),
    .AddressFromBus(cpu_1_addresstobus), .LEDs(ledpanelcontroller_1_leds),
    .out_5(ledpanelcontroller_1_out_5), .out_6(ledpanelcontroller_1_out_6),
    .out_7(ledpanelcontroller_1_out_7), .out_8(ledpanelcontroller_1_out_8),
    .out_9(ledpanelcontroller_1_out_9), .out_10(ledpanelcontroller_1_out_10),
    .out_11(ledpanelcontroller_1_out_11));
  // Buzzer #(.waveform("Square")) buzzer_2: pin names not known; wires that end beside it: buzzercontroller_1_frequencydata2, buzzer_1_p2, buzzercontroller_1_volumedata2
  // Buzzer #(.waveform("Triangle")) buzzer_3: pin names not known; wires that end beside it: buzzercontroller_1_frequencydata3, buzzer_1_p2, buzzercontroller_1_volumedata3

  // Notes on the sheet:
  //   Write_enable
  //   Address
  //   Data
endmodule

module CPU (
  input  [31:0] DataFromBus,
  output [25:0] AddressToBus,
  output BusWriteEnable,
  output [31:0] DataToBus
);

  wire alu_1_is_equal, and_1_out, and_2_out, clock_1_out, control_1_imm_sel, control_1_is_beq,
       control_1_is_bne, control_1_is_jal, control_1_is_jr, control_1_is_jump, control_1_mem_select,
       control_1_reg_write_e, not_1_out, or_1_out;
  wire [3:0] control_1_alu_code;
  wire [4:0] control_1_rd, control_1_rs, control_1_rt;
  wire [15:0] bit_extender_3_out, control_1_imm, shifter_1_out;
  wire [25:0] bit_extender_4_out, shifter_2_out;
  wire [31:0] adder_1_out, adder_2_out, alu_1_res, bit_extender_1_out, bit_extender_2_out,
       bit_extender_5_out, multiplexer_1_out, multiplexer_2_out, multiplexer_3_out, multiplexer_4_out,
       multiplexer_5_out, multiplexer_6_out, PC_q, regfile_1_rs_data, rom_1_data, shifter_3_out;

  Shifter #(.width(16)) shifter_1 (.in(control_1_imm), .\dist (4'b0010), .out(shifter_1_out));
  Adder #(.width(32)) adder_1 (.a(PC_q), .b(32'h4), .out(adder_1_out));  // open: cin, cout
  Adder #(.width(32)) adder_2 (.a(adder_1_out), .b(bit_extender_1_out), .out(adder_2_out));  // open: cin, cout
  assign bit_extender_1_out = {{16{shifter_1_out[15]}}, shifter_1_out};  // Bit_Extender bit_extender_1
  Multiplexer #(.width(32)) multiplexer_1 (
    .in0(adder_1_out), .in1(adder_2_out), .out(multiplexer_1_out), .sel(or_1_out));
  Shifter #(.width(26)) shifter_2 (.in(bit_extender_4_out), .\dist (5'b00010), .out(shifter_2_out));
  Multiplexer #(.width(32)) multiplexer_2 (
    .in0(multiplexer_1_out), .in1(multiplexer_3_out), .out(multiplexer_2_out), .sel(control_1_is_jump));
  assign bit_extender_2_out = {{6{shifter_2_out[25]}}, shifter_2_out};  // Bit_Extender bit_extender_2
  Multiplexer #(.width(32)) multiplexer_3 (
    .in0(bit_extender_2_out), .in1(regfile_1_rs_data), .out(multiplexer_3_out), .sel(control_1_is_jr));
  Shifter #(.shift("lr"), .width(32)) shifter_3 (.in(PC_q), .\dist (5'b00010), .out(shifter_3_out));
  Register #(.width(32)) PC (.D(multiplexer_2_out), .en(1'b1), .clk(clock_1_out), .Q(PC_q));  // open: clr
  Clock clock_1 (.out(clock_1_out));
  Bit_Extender #(.in_width(32)) bit_extender_3 (.in(shifter_3_out), .out(bit_extender_3_out));
  ROM #(.addrWidth(16), .dataWidth(32)) rom_1 (.addr(bit_extender_3_out), .data(rom_1_data));
  // Probe on rom_1_data
  Bit_Extender #(.in_width(32), .out_width(26)) bit_extender_4 (.in(rom_1_data), .out(bit_extender_4_out));
  or or_1 (or_1_out, and_1_out, and_2_out);
  Multiplexer #(.width(32)) multiplexer_4 (
    .in0(alu_1_res), .in1(DataFromBus), .out(multiplexer_4_out), .sel(control_1_mem_select));
  and and_1 (and_1_out, control_1_is_bne, not_1_out);
  and and_2 (and_2_out, control_1_is_beq, alu_1_is_equal);
  Multiplexer #(.width(32)) multiplexer_5 (
    .in0(multiplexer_4_out), .in1(adder_1_out), .out(multiplexer_5_out), .sel(control_1_is_jal));
  not not_1 (not_1_out, alu_1_is_equal);
  Control control_1 (
    .Inst(rom_1_data), .imm(control_1_imm), .rd(control_1_rd), .rt(control_1_rt), .rs(control_1_rs),
    .reg_write_e(control_1_reg_write_e), .ALU_code(control_1_alu_code), .imm_sel(control_1_imm_sel),
    .we_mem(BusWriteEnable), .is_jump(control_1_is_jump), .is_jr(control_1_is_jr), .is_bne(control_1_is_bne),
    .is_beq(control_1_is_beq), .is_jal(control_1_is_jal), .mem_select(control_1_mem_select));
  regfile regfile_1 (
    .write_e(control_1_reg_write_e), .rs(control_1_rs), .rd(control_1_rd), .rd_data(multiplexer_5_out),
    .rt(control_1_rt), .rs_data(regfile_1_rs_data), .rt_data(DataToBus));
  Multiplexer #(.width(32)) multiplexer_6 (
    .in0(DataToBus), .in1(bit_extender_5_out), .out(multiplexer_6_out), .sel(control_1_imm_sel));
  assign bit_extender_5_out = {{16{control_1_imm[15]}}, control_1_imm};  // Bit_Extender bit_extender_5
  ALU alu_1 (
    .OP1(regfile_1_rs_data), .OP2(multiplexer_6_out), .ALU_CODE(control_1_alu_code), .Res(alu_1_res),
    .is_equal(alu_1_is_equal));
  Bit_Extender #(.in_width(32), .out_width(26)) bit_extender_6 (.in(alu_1_res), .out(AddressToBus));

  // Notes on the sheet:
  //   word addressed
  //   PC+4
  //   PC+4+Offset
  //   word addressed
  //   any jump
  //   jr/jalr
  //   byte addressed
  //   byte addressed
  //   immediate
  //   contents of rom_1 (hex, n*v repeats v):
  //   10400017 201b0001 105b0019 201b0005 105b004c 201b0009 105b0087 201b000a 105b008a 201b000b 105b0089
  //   201b000c 105b0089 201b000e 105b008b 201b000f 105b008b 201b0010 105b008d 201b0011 105b008d 201b0012
  //   105b008d 8000093 23bdf000 201b012c ad1bfc00 80000a6 10800031 23bdffdc afbf0000 afa40004 afa80008
  //   afa9000c afaa0010 afab0014 afac0018 afad001c afae0020 20080000 88482a 11200005 2008ffff 880018 2012
  //   2008002d ac08ff00 200e0001 200a000a 1ca0018 7012 1c4402a 11000001 8000031 200c0000 8e001a 5812 2010
  //   11800001 800003e 11600003 200c0001 216d0030 ac0dff00 1ca001a 7012 15c0fff4 8fae0020 8fad001c
  //   8fac0018 8fab0014 8faa0010 8fa9000c 8fa80008 8fa40004 8fbf0000 23bd0024 8000050 20080030 ac08ff00
  //   3400008 4020 1020 8c0dff10 11a0fffe 8c0aff14 2009002d 15490006 20080001 ac08ff10 800005b 8c0dff10
  //   11a0fffe 8c0aff14 20090030 15490002 200b0000 8000085 20090031 15490002 200b0001 8000085 20090032
  //   15490002 200b0002 8000085 20090033 15490002 200b0003 8000085 20090034 15490002 200b0004 8000085
  //   20090035 15490002 200b0005 8000085 20090036 15490002 200b0006 8000085 20090037 15490002 200b0007
  //   8000085 20090038 15490002 200b0008 8000085 20090039 15490007 200b0009 ac08ff10 200c000a 4c0018 1012
  //   4b1020 800005b 11000001 21022 3400008 8d08fc00 81020 884020 ad08fc00 3400008 8000093 ac04ff00
  //   3400008 8c08ff10 1100fffe 8c02ff14 3400008 ac04ff30 3400008 ac04ff38 ac05ff34 ac06ff2c 3400008
  //   8c02ff3c 3400008 8c02ff40 3400008 ac04ff44 3400008 20100000 20110064 201200c8 8e050000 8e240000
  //   8e460000 8e460000 22100004 22310004 22520004 22520004 2002000f d00c 20040001 2002000e d00c 14c0fff2
  //   20040000 2002000e d00c 80000a9
  //   RS Data
  //   target label
  //   ALU
  //   Mem
  //   PC+4
  //   Jalr/Jal
endmodule

module MemoryController (
  input  WriteEnableFromBus,
  input  [25:0] AddressFromBus,
  input  [31:0] DataFromBus,
  input  [31:0] DataFromMem,
  output [31:0] DataToBus,
  output WriteToBus,
  output WriteEnableToMem,
  output [23:0] AddressToMem,
  output [31:0] DataToMem
);

  wire comparator_1_lt, not_1_out;
  wire [25:0] shifter_1_out;

  Comparator #(.mode("unsigned"), .width(26)) comparator_1 (
    .a(AddressFromBus), .b(26'h3ffff00), .lt(comparator_1_lt));  // open: gt, eq
  not not_1 (not_1_out, WriteEnableFromBus);
  and and_1 (WriteToBus, not_1_out, comparator_1_lt);
  and and_2 (WriteEnableToMem, WriteEnableFromBus, comparator_1_lt);
  Bit_Extender #(.in_width(26), .out_width(24), .\type ("zero")) bit_extender_1 (
    .in(shifter_1_out), .out(AddressToMem));
  Shifter #(.shift("lr"), .width(26)) shifter_1 (.in(AddressFromBus), .\dist (5'b00010), .out(shifter_1_out));

  assign DataToBus = DataFromMem;
  assign DataToMem = DataFromBus;
endmodule

module KeyboardController (
  input  [25:0] AddressFromBus,
  input  WriteEnableFromBus,
  input  KeyboardStatus,
  input  [6:0] KeyboardData,
  input  [31:0] DataFromBus,
  output KeyboardRead,
  output [31:0] DataToBus,
  output WriteToBus
);

  wire and_2_out, and_3_out, comparator_1_eq, comparator_2_eq, multiplexer_1_out, not_1_out;
  wire [31:0] bit_extender_1_out, bit_extender_2_out;

  Comparator #(.width(26)) comparator_1 (.a(AddressFromBus), .b(26'h3ffff10), .eq(comparator_1_eq));  // open: gt, lt
  Comparator #(.width(26)) comparator_2 (.a(AddressFromBus), .b(26'h3ffff14), .eq(comparator_2_eq));  // open: gt, lt
  Multiplexer multiplexer_1 (.in1(KeyboardStatus), .out(multiplexer_1_out), .sel(and_2_out));  // open: in0
  not not_1 (not_1_out, WriteEnableFromBus);
  assign bit_extender_1_out = {{31{1'b0}}, multiplexer_1_out};  // Bit_Extender bit_extender_1
  assign bit_extender_2_out = {{25{1'b0}}, KeyboardData};  // Bit_Extender bit_extender_2
  and and_1 (KeyboardRead, comparator_1_eq, WriteEnableFromBus);
  and and_2 (and_2_out, comparator_1_eq, not_1_out);
  and and_3 (and_3_out, comparator_2_eq, not_1_out);
  Multiplexer #(.width(32)) multiplexer_2 (
    .in0(bit_extender_1_out), .in1(bit_extender_2_out), .out(DataToBus), .sel(and_3_out));
  or or_1 (WriteToBus, and_2_out, and_3_out);
endmodule

module RGBController (
  input  [25:0] AddressFromBus,
  input  [31:0] DataFromBus,
  input  WriteEnable,
  output [7:0] RGBX,
  output [7:0] RGBY,
  output [23:0] RGBColor,
  output RGBWrite
);

  wire and_1_out, and_2_out, and_3_out, clock_1_out, comparator_1_eq, comparator_2_eq, comparator_3_eq,
       comparator_4_eq;
  wire [31:0] Color_q, InternalX_q, InternalY_q;

  Comparator #(.width(26)) comparator_1 (.a(AddressFromBus), .b(26'h3ffff20), .eq(comparator_1_eq));  // open: gt, lt
  Comparator #(.width(26)) comparator_2 (.a(AddressFromBus), .b(26'h3ffff24), .eq(comparator_2_eq));  // open: gt, lt
  Comparator #(.width(26)) comparator_3 (.a(AddressFromBus), .b(26'h3ffff28), .eq(comparator_3_eq));  // open: gt, lt
  Comparator #(.width(26)) comparator_4 (.a(AddressFromBus), .b(26'h3ffff2c), .eq(comparator_4_eq));  // open: gt, lt
  and and_1 (and_1_out, comparator_1_eq, WriteEnable);
  and and_2 (and_2_out, comparator_2_eq, WriteEnable);
  and and_3 (and_3_out, comparator_3_eq, WriteEnable);
  and and_4 (RGBWrite, comparator_4_eq, WriteEnable);
  Register #(.width(32)) InternalX (.D(DataFromBus), .en(and_1_out), .clk(clock_1_out), .Q(InternalX_q));  // open: clr
  Register #(.width(32)) InternalY (.D(DataFromBus), .en(and_2_out), .clk(clock_1_out), .Q(InternalY_q));  // open: clr
  Register #(.width(32)) Color (.D(DataFromBus), .en(and_3_out), .clk(clock_1_out), .Q(Color_q));  // open: clr
  Clock clock_1 (.out(clock_1_out));
  Bit_Extender #(.in_width(32), .out_width(8), .\type ("zero")) bit_extender_1 (.in(InternalX_q), .out(RGBX));
  Bit_Extender #(.in_width(32), .out_width(8), .\type ("zero")) bit_extender_2 (.in(InternalY_q), .out(RGBY));
  Bit_Extender #(.in_width(32), .out_width(24), .\type ("zero")) bit_extender_3 (.in(Color_q), .out(RGBColor));
endmodule

module TerminalController (
  input  WriteEnableFromBus,
  input  [25:0] AddressFromBus,
  input  [31:0] DataFromBus,
  output [6:0] DataToTerminal,
  output WriteToTerminal
);

  wire comparator_1_eq;

  Comparator #(.width(26)) comparator_1 (.a(AddressFromBus), .b(26'h3ffff00), .eq(comparator_1_eq));  // open: gt, lt
  and and_1 (WriteToTerminal, comparator_1_eq, WriteEnableFromBus);

  assign DataToTerminal = DataFromBus[6:0];
endmodule

module Control (
  input  [31:0] Inst,
  output [15:0] imm,
  output [4:0] rd,
  output [4:0] rt,
  output [4:0] rs,
  output reg_write_e,
  output [3:0] ALU_code,
  output imm_sel,
  output we_mem,
  output is_jump,
  output is_jr,
  output is_bne,
  output is_beq,
  output is_jal,
  output mem_select
);

  wire comparator_1_eq, comparator_2_eq, comparator_7_eq, comparator_8_eq, comparator_9_eq, comparator_10_eq,
       comparator_11_eq, comparator_12_eq, comparator_13_eq, comparator_14_eq, comparator_15_eq,
       comparator_16_eq, comparator_17_eq, comparator_18_eq, comparator_19_eq, comparator_20_eq,
       comparator_21_eq, comparator_22_eq, comparator_23_eq, comparator_24_eq, not_1_out, not_2_out,
       not_3_out, not_4_out, not_5_out, not_6_out, or_1_out, or_2_out, or_3_out, or_4_out, or_5_out,
       or_6_out, or_7_out;
  wire [3:0] multiplexer_6_out, multiplexer_7_out, multiplexer_8_out, multiplexer_9_out, multiplexer_10_out,
       multiplexer_11_out, multiplexer_12_out, multiplexer_13_out, multiplexer_14_out, multiplexer_15_out,
       multiplexer_16_out, multiplexer_17_out, multiplexer_18_out;
  wire [4:0] multiplexer_1_out;
  wire [5:0] multiplexer_5_out;
  wire [15:0] bit_extender_1_out;

  assign bit_extender_1_out = {{11{Inst[10]}}, Inst[10:6]};  // Bit_Extender bit_extender_1
  Multiplexer #(.width(5)) multiplexer_1 (
    .in0(Inst[15:11]), .in1(Inst[20:16]), .out(multiplexer_1_out), .sel(or_1_out));
  Multiplexer #(.width(5)) multiplexer_2 (.in0(Inst[25:21]), .in1(Inst[20:16]), .out(rs), .sel(or_5_out));
  or or_1 (or_1_out, mem_select, comparator_7_eq);
  Comparator #(.width(6)) comparator_1 (.a(Inst[31:26]), .b(6'b000010), .eq(comparator_1_eq));  // open: gt, lt
  Comparator #(.width(6)) comparator_2 (.a(Inst[31:26]), .b(6'b000011), .eq(comparator_2_eq));  // open: gt, lt
  Comparator #(.width(6)) comparator_3 (.a(Inst[31:26]), .b(6'b101011), .eq(we_mem));  // open: gt, lt
  Comparator #(.width(6)) comparator_4 (.a(Inst[31:26]), .b(6'b100011), .eq(mem_select));  // open: gt, lt
  Comparator #(.width(6)) comparator_5 (.a(Inst[31:26]), .b(6'b000100), .eq(is_beq));  // open: gt, lt
  Comparator #(.width(6)) comparator_6 (.a(Inst[31:26]), .b(6'b000101), .eq(is_bne));  // open: gt, lt
  Comparator #(.width(6)) comparator_7 (.a(Inst[31:26]), .b(6'b001000), .eq(comparator_7_eq));  // open: gt, lt
  Multiplexer #(.width(16)) multiplexer_3 (.in0(Inst[15:0]), .in1(bit_extender_1_out), .out(imm), .sel(or_5_out));
  Multiplexer #(.width(5)) multiplexer_4 (.in0(multiplexer_1_out), .in1({5{1'b1}}), .out(rd), .sel(comparator_2_eq));
  Comparator #(.width(6)) comparator_8 (.a(multiplexer_5_out), .b(6'b001100), .eq(comparator_8_eq));  // open: gt, lt
  Comparator #(.width(6)) comparator_9 (.a(multiplexer_5_out), .b(6'b001001), .eq(comparator_9_eq));  // open: gt, lt
  Comparator #(.width(6)) comparator_10 (.a(multiplexer_5_out), .b(6'b001000), .eq(comparator_10_eq));  // open: gt, lt
  Comparator #(.width(6)) comparator_11 (.a({6{1'b0}}), .b(Inst[31:26]), .eq(comparator_11_eq));  // open: gt, lt
  or or_2 (or_2_out, we_mem, mem_select);
  Multiplexer #(.width(6)) multiplexer_5 (.in0(Inst[5:0]), .in1(6'b000001), .out(multiplexer_5_out), .sel(or_6_out));
  or or_3 (or_3_out, comparator_1_eq, comparator_2_eq);
  or or_4 (or_4_out, or_2_out, is_beq, is_bne, comparator_7_eq);
  Comparator #(.width(6)) comparator_12 (.a(multiplexer_5_out), .b(6'b100000), .eq(comparator_12_eq));  // open: gt, lt
  Comparator #(.width(6)) comparator_13 (.a(multiplexer_5_out), .b(6'b100010), .eq(comparator_13_eq));  // open: gt, lt
  Comparator #(.width(6)) comparator_14 (.a(multiplexer_5_out), .b(6'b011000), .eq(comparator_14_eq));  // open: gt, lt
  Comparator #(.width(6)) comparator_15 (.a(multiplexer_5_out), .b(6'b011010), .eq(comparator_15_eq));  // open: gt, lt
  Comparator #(.width(6)) comparator_16 (.a(multiplexer_5_out), .b(6'b010010), .eq(comparator_16_eq));  // open: gt, lt
  Comparator #(.width(6)) comparator_17 (.a(multiplexer_5_out), .b(6'b010000), .eq(comparator_17_eq));  // open: gt, lt
  Comparator #(.width(6)) comparator_18 (.a(multiplexer_5_out), .b({6{1'b0}}), .eq(comparator_18_eq));  // open: gt, lt
  Comparator #(.width(6)) comparator_19 (.a(multiplexer_5_out), .b(6'b000010), .eq(comparator_19_eq));  // open: gt, lt
  Comparator #(.width(6)) comparator_20 (.a(multiplexer_5_out), .b(6'b101010), .eq(comparator_20_eq));  // open: gt, lt
  Comparator #(.width(6)) comparator_21 (.a(multiplexer_5_out), .b(6'b100100), .eq(comparator_21_eq));  // open: gt, lt
  Comparator #(.width(6)) comparator_22 (.a(multiplexer_5_out), .b(6'b100101), .eq(comparator_22_eq));  // open: gt, lt
  Comparator #(.width(6)) comparator_23 (.a(multiplexer_5_out), .b(6'b100110), .eq(comparator_23_eq));  // open: gt, lt
  Comparator #(.width(6)) comparator_24 (.a(multiplexer_5_out), .b(6'b100111), .eq(comparator_24_eq));  // open: gt, lt
  Multiplexer #(.width(4)) multiplexer_6 (.in1(4'b0000), .out(multiplexer_6_out), .sel(comparator_12_eq));  // open: in0
  Multiplexer #(.width(4)) multiplexer_7 (
    .in0(multiplexer_6_out), .in1(4'b0001), .out(multiplexer_7_out), .sel(comparator_13_eq));
  Multiplexer #(.width(4)) multiplexer_8 (
    .in0(multiplexer_7_out), .in1(4'b0010), .out(multiplexer_8_out), .sel(comparator_14_eq));
  Multiplexer #(.width(4)) multiplexer_9 (
    .in0(multiplexer_8_out), .in1(4'b0011), .out(multiplexer_9_out), .sel(comparator_15_eq));
  Multiplexer #(.width(4)) multiplexer_10 (
    .in0(multiplexer_9_out), .in1(4'b0100), .out(multiplexer_10_out), .sel(comparator_16_eq));
  or or_5 (or_5_out, comparator_18_eq, comparator_19_eq);
  or or_6 (or_6_out, or_3_out, or_4_out);
  or or_7 (or_7_out, comparator_7_eq, or_2_out);
  Multiplexer #(.width(4)) multiplexer_11 (
    .in0(multiplexer_10_out), .in1(4'b0101), .out(multiplexer_11_out), .sel(comparator_17_eq));
  Multiplexer #(.width(4)) multiplexer_12 (
    .in0(multiplexer_11_out), .in1(4'b0111), .out(multiplexer_12_out), .sel(comparator_18_eq));
  Multiplexer #(.width(4)) multiplexer_13 (
    .in0(multiplexer_12_out), .in1(4'b1000), .out(multiplexer_13_out), .sel(comparator_19_eq));
  Multiplexer #(.width(4)) multiplexer_14 (
    .in0(multiplexer_13_out), .in1(4'b0110), .out(multiplexer_14_out), .sel(comparator_20_eq));
  Multiplexer #(.width(4)) multiplexer_15 (
    .in0(multiplexer_14_out), .in1(4'b1001), .out(multiplexer_15_out), .sel(comparator_21_eq));
  Multiplexer #(.width(4)) multiplexer_16 (
    .in0(multiplexer_15_out), .in1(4'b1010), .out(multiplexer_16_out), .sel(comparator_22_eq));
  Multiplexer #(.width(4)) multiplexer_17 (
    .in0(multiplexer_16_out), .in1(4'b1011), .out(multiplexer_17_out), .sel(comparator_23_eq));
  Multiplexer #(.width(4)) multiplexer_18 (
    .in0(multiplexer_17_out), .in1(4'b1100), .out(multiplexer_18_out), .sel(comparator_24_eq));
  Multiplexer #(.width(4)) multiplexer_19 (
    .in0(multiplexer_18_out), .in1(4'b0000), .out(ALU_code), .sel(comparator_7_eq));
  or or_8 (imm_sel, or_5_out, or_7_out);
  or or_9 (is_jal, comparator_8_eq, comparator_9_eq, comparator_2_eq);
  or or_10 (is_jump, is_jal, comparator_10_eq, comparator_1_eq);
  or or_11 (is_jr, comparator_9_eq, comparator_8_eq, comparator_10_eq);
  not not_1 (not_1_out, comparator_15_eq);
  not not_2 (not_2_out, comparator_14_eq);
  not not_3 (not_3_out, is_beq);
  not not_4 (not_4_out, is_bne);
  not not_5 (not_5_out, comparator_1_eq);
  not not_6 (not_6_out, comparator_10_eq);
  and and_1 (reg_write_e, not_1_out, not_2_out, not_3_out, not_4_out, not_5_out, not_6_out);

  assign rt = Inst[20:16];

  // Notes on the sheet:
  //   Inst: initial=0x18d5822
  //   31:26
  //   j
  //   jal
  //   sw
  //   lw
  //   beq
  //   bne
  //   addi
  //   jal
  //   syscall
  //   jalr
  //   jr
  //   addi or lw
  //   5:0
  //   sw OR lw
  //   Not R-Type Instruction
  //   J-Type Instruction
  //   I-Type Instruction
  //   Addi Instruction
  //   sll OR srl
  //   addi OR lw OR sw
  //   jal/syscall/jalr
  //   any jump
  //   jr/jalr
  //   This should be 1 unless instr is
  //   mult, div, beq, bne, j, jr
endmodule

module ALU (
  input  [31:0] OP1,
  input  [31:0] OP2,
  input  [3:0] ALU_CODE,
  output [31:0] Res,
  output is_equal
);

  wire clock_1_out, comparator_1_lt, demultiplexer_1_out2, demultiplexer_1_out3, or_2_out;
  wire [31:0] adder_1_out, and_1_out, bit_extender_1_out, divider_1_out, divider_1_rem, HI_q, LO_q,
       multiplexer_1_out, multiplexer_2_out, multiplier_1_cout, multiplier_1_out, nor_1_out, or_1_out,
       shifter_1_out, shifter_2_out, subtractor_1_out, xor_1_out;

  Demultiplexer #(.select(4)) demultiplexer_1 (
    .out2(demultiplexer_1_out2), .out3(demultiplexer_1_out3), .in(1'b1), .sel(ALU_CODE));  // open: out0, out1, out4, out5, out6, out7, out8, out9, out10, out11, out12, out13, out14, out15
  Adder #(.width(32)) adder_1 (.a(OP1), .b(OP2), .out(adder_1_out));  // open: cin, cout
  Subtractor #(.width(32)) subtractor_1 (.a(OP1), .b(OP2), .out(subtractor_1_out));  // open: bin, bout
  Multiplier #(.width(32)) multiplier_1 (
    .a(OP1), .b(OP2), .out(multiplier_1_out), .cout(multiplier_1_cout));  // open: cin
  Divider #(.width(32)) divider_1 (.a(OP1), .b(OP2), .out(divider_1_out), .rem(divider_1_rem));  // open: upper
  Comparator #(.width(32)) comparator_1 (.a(OP1), .b(OP2), .eq(is_equal), .lt(comparator_1_lt));  // open: gt
  Shifter #(.width(32)) shifter_1 (.in(OP1), .\dist (OP2[4:0]), .out(shifter_1_out));
  Shifter #(.shift("lr"), .width(32)) shifter_2 (.in(OP1), .\dist (OP2[4:0]), .out(shifter_2_out));
  assign bit_extender_1_out = {{31{1'b0}}, comparator_1_lt};  // Bit_Extender bit_extender_1
  assign and_1_out = OP1 & OP2;  // AND_Gate and_1, 32 bits wide
  assign or_1_out = OP1 | OP2;  // OR_Gate or_1, 32 bits wide
  assign xor_1_out = OP1 ^ OP2;  // XOR_Gate xor_1, 32 bits wide
  assign nor_1_out = ~(OP1 | OP2);  // NOR_Gate nor_1, 32 bits wide
  Multiplexer #(.width(32)) multiplexer_1 (
    .in0(multiplier_1_cout), .in1(divider_1_rem), .out(multiplexer_1_out), .sel(demultiplexer_1_out3));
  Multiplexer #(.width(32)) multiplexer_2 (
    .in0(multiplier_1_out), .in1(divider_1_out), .out(multiplexer_2_out), .sel(demultiplexer_1_out3));
  Register #(.width(32)) HI (.D(multiplexer_1_out), .en(or_2_out), .clk(clock_1_out), .Q(HI_q));  // open: clr
  or or_2 (or_2_out, demultiplexer_1_out2, demultiplexer_1_out3);
  Register #(.width(32)) LO (.D(multiplexer_2_out), .en(or_2_out), .clk(clock_1_out), .Q(LO_q));  // open: clr
  Clock clock_1 (.out(clock_1_out));
  Multiplexer #(.select(4), .width(32)) multiplexer_3 (
    .in0(adder_1_out), .in1(subtractor_1_out), .in4(LO_q), .in5(HI_q), .in6(bit_extender_1_out),
    .in7(shifter_1_out), .in8(shifter_2_out), .in9(and_1_out), .in10(or_1_out), .in11(xor_1_out),
    .in12(nor_1_out), .out(Res), .sel(ALU_CODE));  // open: in2, in3, in13, in14, in15

  // Notes on the sheet:
  //   Part above will be trying to put in mult results a lot
  //   but it will not have write enable so it wont
endmodule

module regfile (
  input  write_e,
  input  [4:0] rs,
  input  [4:0] rd,
  input  [31:0] rd_data,
  input  [4:0] rt,
  output [31:0] rs_data,
  output [31:0] rt_data
);

  wire clock_1_out, demultiplexer_1_out1, demultiplexer_1_out2, demultiplexer_1_out3, demultiplexer_1_out4,
       demultiplexer_1_out5, demultiplexer_1_out6, demultiplexer_1_out7, demultiplexer_1_out8,
       demultiplexer_1_out9, demultiplexer_1_out10, demultiplexer_1_out11, demultiplexer_1_out12,
       demultiplexer_1_out13, demultiplexer_1_out14, demultiplexer_1_out15, demultiplexer_1_out16,
       demultiplexer_1_out17, demultiplexer_1_out18, demultiplexer_1_out19, demultiplexer_1_out20,
       demultiplexer_1_out21, demultiplexer_1_out22, demultiplexer_1_out23, demultiplexer_1_out24,
       demultiplexer_1_out25, demultiplexer_1_out26, demultiplexer_1_out27, demultiplexer_1_out28,
       demultiplexer_1_out29, demultiplexer_1_out30, demultiplexer_1_out31;
  wire [31:0] reg1_q, reg2_q, reg3_q, reg4_q, reg5_q, reg6_q, reg7_q, reg8_q, reg9_q, reg10_q, reg11_q,
       reg12_q, reg13_q, reg14_q, reg15_q, reg16_q, reg17_q, reg18_q, reg19_q, reg20_q, reg21_q, reg22_q,
       reg23_q, reg24_q, reg25_q, reg26_q, reg27_q, reg28_q, reg29_q, reg30_q, reg31_q;

  Demultiplexer #(.select(5)) demultiplexer_1 (
    .out1(demultiplexer_1_out1), .out2(demultiplexer_1_out2), .out3(demultiplexer_1_out3),
    .out4(demultiplexer_1_out4), .out5(demultiplexer_1_out5), .out6(demultiplexer_1_out6),
    .out7(demultiplexer_1_out7), .out8(demultiplexer_1_out8), .out9(demultiplexer_1_out9),
    .out10(demultiplexer_1_out10), .out11(demultiplexer_1_out11), .out12(demultiplexer_1_out12),
    .out13(demultiplexer_1_out13), .out14(demultiplexer_1_out14), .out15(demultiplexer_1_out15),
    .out16(demultiplexer_1_out16), .out17(demultiplexer_1_out17), .out18(demultiplexer_1_out18),
    .out19(demultiplexer_1_out19), .out20(demultiplexer_1_out20), .out21(demultiplexer_1_out21),
    .out22(demultiplexer_1_out22), .out23(demultiplexer_1_out23), .out24(demultiplexer_1_out24),
    .out25(demultiplexer_1_out25), .out26(demultiplexer_1_out26), .out27(demultiplexer_1_out27),
    .out28(demultiplexer_1_out28), .out29(demultiplexer_1_out29), .out30(demultiplexer_1_out30),
    .out31(demultiplexer_1_out31), .in(write_e), .sel(rd));  // open: out0
  Clock clock_1 (.out(clock_1_out));
  Register #(.width(32)) reg1 (.D(rd_data), .en(demultiplexer_1_out1), .clk(clock_1_out), .Q(reg1_q));  // open: clr
  Register #(.width(32)) reg13 (.D(rd_data), .en(demultiplexer_1_out13), .clk(clock_1_out), .Q(reg13_q));  // open: clr
  Register #(.width(32)) reg25 (.D(rd_data), .en(demultiplexer_1_out25), .clk(clock_1_out), .Q(reg25_q));  // open: clr
  Register #(.width(32)) reg2 (.D(rd_data), .en(demultiplexer_1_out2), .clk(clock_1_out), .Q(reg2_q));  // open: clr
  Register #(.width(32)) reg14 (.D(rd_data), .en(demultiplexer_1_out14), .clk(clock_1_out), .Q(reg14_q));  // open: clr
  Register #(.width(32)) reg26 (.D(rd_data), .en(demultiplexer_1_out26), .clk(clock_1_out), .Q(reg26_q));  // open: clr
  Register #(.width(32)) reg27 (.D(rd_data), .en(demultiplexer_1_out27), .clk(clock_1_out), .Q(reg27_q));  // open: clr
  Register #(.width(32)) reg3 (.D(rd_data), .en(demultiplexer_1_out3), .clk(clock_1_out), .Q(reg3_q));  // open: clr
  Register #(.width(32)) reg15 (.D(rd_data), .en(demultiplexer_1_out15), .clk(clock_1_out), .Q(reg15_q));  // open: clr
  Register #(.width(32)) reg4 (.D(rd_data), .en(demultiplexer_1_out4), .clk(clock_1_out), .Q(reg4_q));  // open: clr
  Register #(.width(32)) reg16 (.D(rd_data), .en(demultiplexer_1_out16), .clk(clock_1_out), .Q(reg16_q));  // open: clr
  Register #(.width(32)) reg28 (.D(rd_data), .en(demultiplexer_1_out28), .clk(clock_1_out), .Q(reg28_q));  // open: clr
  Register #(.width(32)) reg5 (.D(rd_data), .en(demultiplexer_1_out5), .clk(clock_1_out), .Q(reg5_q));  // open: clr
  Register #(.width(32)) reg17 (.D(rd_data), .en(demultiplexer_1_out17), .clk(clock_1_out), .Q(reg17_q));  // open: clr
  Register #(.width(32)) reg29 (.D(rd_data), .en(demultiplexer_1_out29), .clk(clock_1_out), .Q(reg29_q));  // open: clr
  Register #(.width(32)) reg6 (.D(rd_data), .en(demultiplexer_1_out6), .clk(clock_1_out), .Q(reg6_q));  // open: clr
  Register #(.width(32)) reg18 (.D(rd_data), .en(demultiplexer_1_out18), .clk(clock_1_out), .Q(reg18_q));  // open: clr
  Register #(.width(32)) reg30 (.D(rd_data), .en(demultiplexer_1_out30), .clk(clock_1_out), .Q(reg30_q));  // open: clr
  Register #(.width(32)) reg7 (.D(rd_data), .en(demultiplexer_1_out7), .clk(clock_1_out), .Q(reg7_q));  // open: clr
  Register #(.width(32)) reg19 (.D(rd_data), .en(demultiplexer_1_out19), .clk(clock_1_out), .Q(reg19_q));  // open: clr
  Register #(.width(32)) reg31 (.D(rd_data), .en(demultiplexer_1_out31), .clk(clock_1_out), .Q(reg31_q));  // open: clr
  Register #(.width(32)) reg8 (.D(rd_data), .en(demultiplexer_1_out8), .clk(clock_1_out), .Q(reg8_q));  // open: clr
  Register #(.width(32)) reg20 (.D(rd_data), .en(demultiplexer_1_out20), .clk(clock_1_out), .Q(reg20_q));  // open: clr
  Register #(.width(32)) reg9 (.D(rd_data), .en(demultiplexer_1_out9), .clk(clock_1_out), .Q(reg9_q));  // open: clr
  Register #(.width(32)) reg21 (.D(rd_data), .en(demultiplexer_1_out21), .clk(clock_1_out), .Q(reg21_q));  // open: clr
  Register #(.width(32)) reg10 (.D(rd_data), .en(demultiplexer_1_out10), .clk(clock_1_out), .Q(reg10_q));  // open: clr
  Register #(.width(32)) reg22 (.D(rd_data), .en(demultiplexer_1_out22), .clk(clock_1_out), .Q(reg22_q));  // open: clr
  Register #(.width(32)) reg11 (.D(rd_data), .en(demultiplexer_1_out11), .clk(clock_1_out), .Q(reg11_q));  // open: clr
  Register #(.width(32)) reg23 (.D(rd_data), .en(demultiplexer_1_out23), .clk(clock_1_out), .Q(reg23_q));  // open: clr
  Register #(.width(32)) reg12 (.D(rd_data), .en(demultiplexer_1_out12), .clk(clock_1_out), .Q(reg12_q));  // open: clr
  Register #(.width(32)) reg24 (.D(rd_data), .en(demultiplexer_1_out24), .clk(clock_1_out), .Q(reg24_q));  // open: clr
  Multiplexer #(.select(5), .width(32)) multiplexer_1 (
    .in0({32{1'b0}}), .in1(reg1_q), .in2(reg2_q), .in3(reg3_q), .in4(reg4_q), .in5(reg5_q), .in6(reg6_q),
    .in7(reg7_q), .in8(reg8_q), .in9(reg9_q), .in10(reg10_q), .in11(reg11_q), .in12(reg12_q), .in13(reg13_q),
    .in14(reg14_q), .in15(reg15_q), .in16(reg16_q), .in17(reg17_q), .in18(reg18_q), .in19(reg19_q),
    .in20(reg20_q), .in21(reg21_q), .in22(reg22_q), .in23(reg23_q), .in24(reg24_q), .in25(reg25_q),
    .in26(reg26_q), .in27(reg27_q), .in28(reg28_q), .in29(reg29_q), .in30(reg30_q), .in31(reg31_q),
    .out(rs_data), .sel(rs));
  Multiplexer #(.select(5), .width(32)) multiplexer_2 (
    .in0({32{1'b0}}), .in1(reg1_q), .in2(reg2_q), .in3(reg3_q), .in4(reg4_q), .in5(reg5_q), .in6(reg6_q),
    .in7(reg7_q), .in8(reg8_q), .in9(reg9_q), .in10(reg10_q), .in11(reg11_q), .in12(reg12_q), .in13(reg13_q),
    .in14(reg14_q), .in15(reg15_q), .in16(reg16_q), .in17(reg17_q), .in18(reg18_q), .in19(reg19_q),
    .in20(reg20_q), .in21(reg21_q), .in22(reg22_q), .in23(reg23_q), .in24(reg24_q), .in25(reg25_q),
    .in26(reg26_q), .in27(reg27_q), .in28(reg28_q), .in29(reg29_q), .in30(reg30_q), .in31(reg31_q),
    .out(rt_data), .sel(rt));
endmodule

module BuzzerController (
  input  [31:0] DataFromBus,
  input  WriteEnableFromBus,
  input  [25:0] AddressFromBus,
  output [13:0] FrequencyData1,
  output [13:0] FrequencyData2,
  output [13:0] FrequencyData3,
  output WriteToBuzzer,
  output [6:0] VolumeData1,
  output [6:0] VolumeData2,
  output [6:0] VolumeData3
);

  wire and_1_out, and_2_out, and_3_out, and_4_out, clock_1_out, comparator_1_eq, comparator_2_eq,
       comparator_3_eq, comparator_4_eq;
  wire [1:0] TargetBuzzer_q;
  wire [6:0] Volume_q;
  wire [13:0] Frequency_q;

  Comparator #(.width(26)) comparator_1 (.a(AddressFromBus), .b(26'h3ffff30), .eq(comparator_1_eq));  // open: gt, lt
  Comparator #(.width(26)) comparator_2 (.a(AddressFromBus), .b(26'h3ffff34), .eq(comparator_2_eq));  // open: gt, lt
  Comparator #(.width(26)) comparator_3 (.a(AddressFromBus), .b(26'h3ffff38), .eq(comparator_3_eq));  // open: gt, lt
  Comparator #(.width(26)) comparator_4 (.a(AddressFromBus), .b(26'h3ffff2c), .eq(comparator_4_eq));  // open: gt, lt
  and and_1 (and_1_out, WriteEnableFromBus, comparator_1_eq);
  and and_2 (and_2_out, comparator_2_eq, WriteEnableFromBus);
  and and_3 (and_3_out, comparator_3_eq, WriteEnableFromBus);
  and and_4 (and_4_out, comparator_4_eq, WriteEnableFromBus);
  Clock clock_1 (.out(clock_1_out));
  Register #(.width(14)) Frequency (
    .D(DataFromBus[13:0]), .en(and_2_out), .clk(clock_1_out), .Q(Frequency_q));  // open: clr
  Register #(.width(1)) OnOff (.D(DataFromBus[0]), .en(and_1_out), .clk(clock_1_out), .Q(WriteToBuzzer));  // open: clr
  Register #(.width(7)) Volume (.D(DataFromBus[6:0]), .en(and_3_out), .clk(clock_1_out), .Q(Volume_q));  // open: clr
  Register #(.width(2)) TargetBuzzer (
    .D(DataFromBus[1:0]), .en(and_4_out), .clk(clock_1_out), .Q(TargetBuzzer_q));  // open: clr
  Demultiplexer #(.select(2), .width(14)) demultiplexer_1 (
    .out0(FrequencyData1), .out1(FrequencyData2), .out2(FrequencyData3), .in(Frequency_q),
    .sel(TargetBuzzer_q));  // open: out3
  Demultiplexer #(.select(2), .width(7)) demultiplexer_2 (
    .out0(VolumeData1), .out1(VolumeData2), .out2(VolumeData3), .in(Volume_q), .sel(TargetBuzzer_q));  // open: out3
endmodule

module JoyStickController (
  input  WriteEnableFromBus,
  input  [25:0] AddressFromBus,
  input  [3:0] X,
  input  [3:0] Y,
  input  [31:0] DataFromBus,
  output [31:0] DataToBus,
  output WriteEnableToBus
);

  wire and_1_out, and_2_out, comparator_1_eq, comparator_2_eq, not_1_out;

  not not_1 (not_1_out, WriteEnableFromBus);
  Comparator #(.width(26)) comparator_1 (.a(AddressFromBus), .b(26'h3ffff3c), .eq(comparator_1_eq));  // open: gt, lt
  Comparator #(.width(26)) comparator_2 (.a(AddressFromBus), .b(26'h3ffff40), .eq(comparator_2_eq));  // open: gt, lt
  and and_1 (and_1_out, not_1_out, comparator_1_eq);
  and and_2 (and_2_out, not_1_out, comparator_2_eq);
  Multiplexer #(.width(4)) multiplexer_1 (.in0(X), .in1(Y), .out(DataToBus[3:0]), .sel(and_2_out));
  or or_1 (WriteEnableToBus, and_1_out, and_2_out);

  assign DataToBus[31:4] = {28{1'b0}};

  // Notes on the sheet:
  //   AddressFromBus: initial=0x3ffff50
  //   X
  //   Y
endmodule

module LEDPanelController (
  input  [31:0] DataFromBus,
  input  WriteEnableFromBus,
  input  [25:0] AddressFromBus,
  output LEDs,
  output out_5,
  output out_6,
  output out_7,
  output out_8,
  output out_9,
  output out_10,
  output out_11
);

  wire and_1_out, clock_1_out, comparator_1_eq;

  Comparator #(.width(26)) comparator_1 (.a(AddressFromBus), .b(26'h3ffff44), .eq(comparator_1_eq));  // open: gt, lt
  and and_1 (and_1_out, WriteEnableFromBus, comparator_1_eq);
  Clock clock_1 (.out(clock_1_out));
  Register LEDsOn (
    .D(DataFromBus[7:0]), .en(and_1_out), .clk(clock_1_out),
    .Q({out_11, out_10, out_9, out_8, out_7, out_6, out_5, LEDs}));  // open: clr
endmodule

module Buzzer2Controller (
  input  [31:0] DataFromBus,
  input  WriteEnableFromBus,
  input  [25:0] AddressFromBus,
  output [13:0] FrequencyData,
  output WriteToBuzzer,
  output [6:0] VoumeData
);

  wire and_1_out, and_2_out, and_3_out, clock_1_out, comparator_1_eq, comparator_2_eq, comparator_3_eq;

  Comparator #(.width(26)) comparator_1 (.a(AddressFromBus), .b(26'h3ffff20), .eq(comparator_1_eq));  // open: gt, lt
  Comparator #(.width(26)) comparator_2 (.a(AddressFromBus), .b(26'h3ffff24), .eq(comparator_2_eq));  // open: gt, lt
  Comparator #(.width(26)) comparator_3 (.a(AddressFromBus), .b(26'h3ffff28), .eq(comparator_3_eq));  // open: gt, lt
  Register #(.width(14)) Frequency (
    .D(DataFromBus[13:0]), .en(and_2_out), .clk(clock_1_out), .Q(FrequencyData));  // open: clr
  Register #(.width(1)) OnOff (.D(DataFromBus[0]), .en(and_1_out), .clk(clock_1_out), .Q(WriteToBuzzer));  // open: clr
  and and_1 (and_1_out, WriteEnableFromBus, comparator_1_eq);
  and and_2 (and_2_out, comparator_2_eq, WriteEnableFromBus);
  and and_3 (and_3_out, comparator_3_eq, WriteEnableFromBus);
  Register #(.width(7)) Volume (.D(DataFromBus[6:0]), .en(and_3_out), .clk(clock_1_out), .Q(VoumeData));  // open: clr
  Clock clock_1 (.out(clock_1_out));
endmodule

module Buzzer3Controller (
  input  [31:0] DataFromBus,
  input  WriteEnableFromBus,
  input  [25:0] AddressFromBus,
  output [13:0] FrequencyData,
  output WriteToBuzzer,
  output [6:0] VoumeData
);

  wire and_1_out, and_2_out, and_3_out, clock_1_out, comparator_1_eq, comparator_2_eq, comparator_3_eq;

  Comparator #(.width(26)) comparator_1 (.a(AddressFromBus), .b(26'h3ffff10), .eq(comparator_1_eq));  // open: gt, lt
  Comparator #(.width(26)) comparator_2 (.a(AddressFromBus), .b(26'h3ffff14), .eq(comparator_2_eq));  // open: gt, lt
  Comparator #(.width(26)) comparator_3 (.a(AddressFromBus), .b(26'h3ffff18), .eq(comparator_3_eq));  // open: gt, lt
  Register #(.width(14)) Frequency (
    .D(DataFromBus[13:0]), .en(and_2_out), .clk(clock_1_out), .Q(FrequencyData));  // open: clr
  Register #(.width(1)) OnOff (.D(DataFromBus[0]), .en(and_1_out), .clk(clock_1_out), .Q(WriteToBuzzer));  // open: clr
  and and_1 (and_1_out, WriteEnableFromBus, comparator_1_eq);
  and and_2 (and_2_out, comparator_2_eq, WriteEnableFromBus);
  and and_3 (and_3_out, comparator_3_eq, WriteEnableFromBus);
  Register #(.width(7)) Volume (.D(DataFromBus[6:0]), .en(and_3_out), .clk(clock_1_out), .Q(VoumeData));  // open: clr
  Clock clock_1 (.out(clock_1_out));
endmodule
